// Logisim project main.circ as structural Verilog: 1 circuit, main circuit main
module main (
  input  [5:0] in_1,
  input  [1:0] in_2,
  input  in_3,
  input  in_4,
  input  in_5,
  input  in_6,
  input  in_7,
  input  in_8,
  output [1:0] out_9
);

  wire [7:0] gpu_1_out_5, gpu_1_out_6, gpu_1_out_7, gpu_1_out_8, gpu_1_out_9, gpu_1_out_10, gpu_1_out_11,
       gpu_1_out_12;

  RAM #(.addrWidth(6), .dataWidth(2), .bus("separate")) ram_1 (
    .addr(in_1), .din(in_2), .data(out_9), .str(in_3), .sel(in_4), .clk(in_5), .ld(in_6), .clr(in_7));
  GPU gpu_1 (
    .out_5(gpu_1_out_5), .out_6(gpu_1_out_6), .out_7(gpu_1_out_7), .out_8(gpu_1_out_8), .out_9(gpu_1_out_9),
    .out_10(gpu_1_out_10), .out_11(gpu_1_out_11), .out_12(gpu_1_out_12), .in_2(in_8));  // open: in_1, in_3, in_4
  DotMatrix #(.inputtype("row"), .matrixcols(8), .matrixrows(8)) dotmatrix_1 (
    .row0(gpu_1_out_5), .row1(gpu_1_out_6), .row2(gpu_1_out_7), .row3(gpu_1_out_8), .row4(gpu_1_out_9),
    .row5(gpu_1_out_10), .row6(gpu_1_out_11), .row7(gpu_1_out_12));
endmodule
