// Logisim project TETRIS.circ as structural Verilog: 1 circuit, main circuit main
module main (
  input  in_1,
  input  in_2,
  input  in_3
);

  wire tetris_1_p6, tetris_1_p7;
  wire [3:0] tetris_1_p1, tetris_1_p3;
  wire [6:0] tetris_1_p8;

  Hex_Digit_Display hex_digit_display_1 (.value(tetris_1_p1));  // open: dp
  Hex_Digit_Display hex_digit_display_2 (.value(tetris_1_p3));  // open: dp
  DotMatrix #(.inputtype("row"), .matrixcols(8), .matrixrows(16)) dotmatrix_1 ();  // open: row0, row1, row2, row3, row4, row5, row6, row7, row8, row9, row10, row11, row12, row13, row14, row15
  // Tetris tetris_1: pin names not known; wires that end beside it: tetris_1_p1, in_1, tetris_1_p3, in_2, in_3, tetris_1_p6, tetris_1_p7, tetris_1_p8
  Button button_1 ();  // open: out
  Keyboard keyboard_1 (.clr(tetris_1_p6), .avail(tetris_1_p7), .data(tetris_1_p8));  // open: clk, re

  // Notes on the sheet:
  //   1. Poziom trudności
  //   2. Taktowanie
  //   3. Start
endmodule
