// Logisim project main.circ as structural Verilog: 1 circuit, main circuit main
module main (
  output [6:0] out_1,
  output \CZY_RUCH_BYŁ_ZABLOKOWANY ,
  output FINISH_PRZESUW,
  output FINISH_ROT
);

  wire blc_rand_1_game_over, blc_rand_1_out_b, button_1_out, CLK, comparator_1_gt, comparator_4_eq,
       comparator_5_gt, comparator_5_lt, comparator_6_eq, comparator_7_gt, comparator_7_lt, comparator_8_eq,
       d_ff_3_q, deleting_rows_1_p1, deleting_rows_1_p5, Deleting_Rows_CLK, demultiplexer_2_out0,
       demultiplexer_2_out1, demultiplexer_3_out0, demultiplexer_3_out1, demultiplexer_4_out0,
       demultiplexer_4_out1, Game_CLK, gpu_manager_1_out_6, gpu_manager_1_out_7, gpu_manager_1_out_8,
       gpu_manager_1_out_9, keyboard_1_avail, keyboard_manager_1_out_5, keyboard_manager_1_out_6,
       main_1_finish, main_1_ram_clk, main_1_zderzenie, main_2_ram_clk, main_3_ram_clk, main_3_zd,
       main_4_flaga, main_4_flaga_2, main_4_trwajaca_akcja, or_1_out, or_2_out, or_3_out, or_4_out, or_5_out,
       or_6_out, RAM_CLK, Reset_Generating_mux;
  wire [1:0] blc_rand_1_out_d, Data_In, Data_Out, Deleting_Rows_Data_In, Deleting_Rows_Data_Out,
       demultiplexer_1_out2, demultiplexer_1_out4, Game_Data, Game_Data_In, Gpu_Data, main_1_data_out,
       main_2_data_out, main_3_data_out;
  wire [1:1] comparator_2_eq;
  wire [2:0] State_Select;
  wire [6:0] adder_1_out, Adress, blc_rand_1_out_a, Deleting_Rows_Adress, Game_Adress, GPU_Adress,
       gpu_manager_1_out_5, keyboard_1_data, keyboard_manager_1_out_4, main_1_a, main_2_a, main_2_nowe_a1,
       main_3_a, multiplexer_1_out, multiplexer_2_out;
  wire [7:0] gpu_1_p5, gpu_1_p6, gpu_1_p7, gpu_1_p8, gpu_1_p9, gpu_1_p10, gpu_1_p11, gpu_1_p12, gpu_1_p13,
       gpu_1_p14, gpu_1_p15, gpu_1_p16, gpu_1_p17, gpu_1_p18, gpu_1_p19, gpu_1_p20;

  Demultiplexer #(.select(3), .width(2)) demultiplexer_1 (
    .out1(Gpu_Data), .out2(demultiplexer_1_out2), .out3(Game_Data), .out4(demultiplexer_1_out4),
    .out5(Deleting_Rows_Data_In), .in(Data_Out), .sel(State_Select));  // open: out0, out6, out7, en
  Comparator #(.width(7), .mode("unsigned")) comparator_1 (
    .a(adder_1_out), .b(7'b1100100), .gt(comparator_1_gt));  // open: eq, lt
  Multiplexer #(.width(7), .disabled(0), .enable("false")) multiplexer_1 (
    .in0(adder_1_out), .in1(out_1), .out(multiplexer_1_out), .sel(comparator_1_gt));
  Comparator #(.width(3), .mode("unsigned")) comparator_2 (
    .a(State_Select), .b(3'b011), .eq(comparator_2_eq[1]));  // open: gt, lt
  Multiplexer #(.select(2), .width(7), .enable("false")) multiplexer_2 (
    .in0(multiplexer_1_out), .in1(7'b0000010), .in2(main_2_nowe_a1), .in3(main_2_nowe_a1),
    .out(multiplexer_2_out), .sel({comparator_2_eq[1], Reset_Generating_mux}));
  Register #(.width(7)) register_1 (.D(multiplexer_2_out), .Q(out_1), .clk(or_1_out), .clr(or_4_out));  // open: en
  or or_1 (or_1_out, blc_rand_1_out_b, FINISH_PRZESUW, demultiplexer_4_out0);
  Adder #(.width(7)) adder_1 (.a(out_1), .b(7'b0001000), .out(adder_1_out));  // open: cin, cout
  Comparator #(.width(3), .mode("unsigned")) comparator_3 (
    .a(State_Select), .b(3'b100), .eq(Reset_Generating_mux));  // open: gt, lt
  Comparator #(.width(3), .mode("unsigned")) comparator_4 (
    .a(State_Select), .b(3'b101), .eq(comparator_4_eq));  // open: gt, lt
  Comparator #(.width(3), .mode("unsigned")) comparator_5 (
    .a(State_Select), .b(3'b011), .gt(comparator_5_gt), .lt(comparator_5_lt));  // open: eq
  or or_2 (or_2_out, comparator_5_gt, comparator_5_lt);
  Comparator #(.width(3), .mode("unsigned")) comparator_6 (
    .a(State_Select), .b(3'b010), .eq(comparator_6_eq));  // open: gt, lt
  or or_3 (or_3_out, comparator_7_gt, comparator_7_lt);
  Comparator #(.width(3), .mode("unsigned")) comparator_7 (
    .a(State_Select), .b(3'b010), .gt(comparator_7_gt), .lt(comparator_7_lt));  // open: eq
  Demultiplexer demultiplexer_2 (
    .out0(demultiplexer_2_out0), .out1(demultiplexer_2_out1), .in(CLK), .sel(main_4_trwajaca_akcja));  // open: en
  Demultiplexer demultiplexer_3 (
    .out0(demultiplexer_3_out0), .out1(demultiplexer_3_out1), .in(comparator_2_eq[1]),
    .sel(main_4_trwajaca_akcja));  // open: en
  BLC_RAND blc_rand_1 (
    .CLK(CLK), .OUT_A(blc_rand_1_out_a), .OUT_D(blc_rand_1_out_d), .START(Reset_Generating_mux),
    .OUT_B(blc_rand_1_out_b), .CURRENT_GAME_ADRESS(blc_rand_1_out_a),
    .CURRENT_GAME_STATE(demultiplexer_1_out4), .GAME_OVER(blc_rand_1_game_over));
  opadanie_main main_1 (
    .A1(out_1), .DATA_IN(demultiplexer_1_out2), .CLK(CLK), .ENABLE(comparator_6_eq),
    .DATA_OUT(main_1_data_out), .A(main_1_a), .RAM_CLK(main_1_ram_clk), .FINISH(main_1_finish),
    .ZDERZENIE(main_1_zderzenie), .RESET(or_3_out));
  Pull_Resistor pull_resistor_1 (.node(or_3_out));
  // Deleting_Rows deleting_rows_1: pin names not known; wires that end beside it: deleting_rows_1_p1, Deleting_Rows_Data_In, comparator_4_eq, CLK, deleting_rows_1_p5, Deleting_Rows_CLK, Deleting_Rows_Adress, Deleting_Rows_Data_Out
  Multiplexer #(.width(7)) multiplexer_3 (
    .in0(main_3_a), .in1(main_2_a), .out(Game_Adress), .sel(main_4_trwajaca_akcja));  // open: en
  D_Flip_Flop d_ff_1 (.clk(main_1_finish), .D(1'b1));  // open: Q, Qn, preset, en, reset
  Pull_Resistor pull_resistor_2 (.node(or_2_out));
  Pull_Resistor pull_resistor_3 (.node(or_2_out));
  D_Flip_Flop d_ff_2 (.clk(blc_rand_1_game_over), .D(1'b1));  // open: Q, Qn, preset, en, reset
  Demultiplexer #(.enable("false")) demultiplexer_4 (
    .out0(demultiplexer_4_out0), .out1(demultiplexer_4_out1), .in(main_1_finish), .sel(d_ff_3_q));
  przesuwanie_main main_2 (
    .A1(out_1), .CLK(demultiplexer_2_out1), .ENABLE(demultiplexer_3_out1), .DATA_IN(Game_Data),
    .FLAGA(main_4_flaga), .NOWE_A1(main_2_nowe_a1), .DATA_OUT(main_2_data_out), .RAM_CLK(main_2_ram_clk),
    .ZD(deleting_rows_1_p1), .A(main_2_a), .FINISH(FINISH_PRZESUW), .RESET(or_2_out));
  rotacja_main main_3 (
    .A1(out_1), .CLK(demultiplexer_2_out0), .ENABLE(demultiplexer_3_out0), .DATA_IN(Game_Data),
    .FLAGA(main_4_flaga_2), .DATA_OUT(main_3_data_out), .RAM_CLK(main_3_ram_clk), .ZD(main_3_zd),
    .A(main_3_a), .FINISH(FINISH_ROT), .RESET(or_2_out));
  Multiplexer #(.select(3), .width(7)) multiplexer_4 (
    .in1(GPU_Adress), .in2(main_1_a), .in3(Game_Adress), .in4(blc_rand_1_out_a), .in5(Deleting_Rows_Adress),
    .out(Adress), .sel(State_Select));  // open: in0, in6, in7, en
  D_Flip_Flop d_ff_3 (
    .clk(main_1_zderzenie), .D(1'b1), .Q(d_ff_3_q), .reset(Reset_Generating_mux));  // open: Qn, preset, en
  Multiplexer multiplexer_5 (
    .in0(main_3_ram_clk), .in1(main_2_ram_clk), .out(Game_CLK), .sel(main_4_trwajaca_akcja));  // open: en
  Multiplexer #(.width(2)) multiplexer_6 (
    .in0(main_3_data_out), .in1(main_2_data_out), .out(Game_Data_In), .sel(main_4_trwajaca_akcja));  // open: en
  Multiplexer #(.select(3), .width(2)) multiplexer_7 (
    .in2(main_1_data_out), .in3(Game_Data_In), .in4(blc_rand_1_out_d), .in5(Deleting_Rows_Data_Out),
    .out(Data_In), .sel(State_Select));  // open: in0, in1, in6, in7, en
  Multiplexer #(.select(3)) multiplexer_8 (
    .in2(main_1_ram_clk), .in3(Game_CLK), .in4(CLK), .in5(Deleting_Rows_CLK), .out(RAM_CLK),
    .sel(State_Select));  // open: in0, in1, in6, in7, en
  Button button_1 (.out(button_1_out));
  or or_4 (or_4_out, button_1_out, demultiplexer_4_out1);
  Keyboard keyboard_1 (
    .clr(keyboard_manager_1_out_5), .avail(keyboard_1_avail), .data(keyboard_1_data));  // open: clk, re
  Clock clock_1 (.out(CLK));
  Keyboard_Manager keyboard_manager_1 (
    .out_4(keyboard_manager_1_out_4), .out_5(keyboard_manager_1_out_5), .in_2(keyboard_1_avail),
    .in_1(keyboard_1_data), .out_6(keyboard_manager_1_out_6), .in_3(or_5_out));
  or or_5 (or_5_out, FINISH_PRZESUW, FINISH_ROT);
  State_Selector state_selector_1 (
    .Keyboard__Input_Happened(keyboard_manager_1_out_6), .out_8(State_Select), .New_Block_Request(or_4_out),
    .Generating_Ended(blc_rand_1_out_b), .Falling_Ended(demultiplexer_4_out0), .Player_Input_Ended(or_6_out),
    .Render(gpu_manager_1_out_9), .Deleting_Rows_Ended(deleting_rows_1_p5));
  Multiplexer multiplexer_9 (
    .in0(main_3_zd), .in1(deleting_rows_1_p1), .out(\CZY_RUCH_BYŁ_ZABLOKOWANY ), .sel(main_4_trwajaca_akcja));  // open: en
  RAM #(.addrWidth(7), .dataWidth(2), .bus("separate")) ram_1 (
    .addr(Adress), .din(Data_In), .data(Data_Out), .clk(RAM_CLK));  // open: str, sel, ld, clr
  or or_6 (or_6_out, FINISH_ROT, FINISH_PRZESUW);
  koder_klawiatura_main main_4 (
    .wejscie_ASCI(keyboard_manager_1_out_4), .FLAGA(main_4_flaga), .FLAGA_2(main_4_flaga_2),
    .TRWAJACA_AKCJA(main_4_trwajaca_akcja));
  Comparator #(.width(3), .mode("unsigned")) comparator_8 (
    .a(State_Select), .b(3'b001), .eq(comparator_8_eq));  // open: gt, lt
  GPU_manager gpu_manager_1 (
    .in_1(Gpu_Data), .out_4(GPU_Adress), .out_5(gpu_manager_1_out_5), .out_6(gpu_manager_1_out_6),
    .out_7(gpu_manager_1_out_7), .out_8(gpu_manager_1_out_8), .out_9(gpu_manager_1_out_9),
    .ENABLE(comparator_8_eq), .in_3(CLK));
  // GPU gpu_1: pin names not known; wires that end beside it: gpu_manager_1_out_5, gpu_manager_1_out_6, gpu_manager_1_out_7, gpu_manager_1_out_8, gpu_1_p5, gpu_1_p6, gpu_1_p7, gpu_1_p8, gpu_1_p9, gpu_1_p10, gpu_1_p11, gpu_1_p12, gpu_1_p13, gpu_1_p14, gpu_1_p15, gpu_1_p16, gpu_1_p17, gpu_1_p18, gpu_1_p19, gpu_1_p20
  DotMatrix #(.inputtype("row"), .matrixcols(8), .matrixrows(16), .dotshape("circle")) dotmatrix_1 (
    .row0(gpu_1_p5), .row1(gpu_1_p6), .row2(gpu_1_p7), .row3(gpu_1_p8), .row4(gpu_1_p9), .row5(gpu_1_p10),
    .row6(gpu_1_p11), .row7(gpu_1_p12), .row8(gpu_1_p13), .row9(gpu_1_p14), .row10(gpu_1_p15),
    .row11(gpu_1_p16), .row12(gpu_1_p17), .row13(gpu_1_p18), .row14(gpu_1_p19), .row15(gpu_1_p20));

  // Notes on the sheet:
  //   CLick to start
  //   ten finisz wystepuje ale od razu sie gasi, bo resetuje tez koder i zmienia flage akcji
endmodule
